// Logisim project alu.circ as structural Verilog: 10 circuits, main circuit alu
module alu (
  input  [31:0] A,
  input  [31:0] B,
  input  [3:0] ALUSel,
  output [31:0] Result
);

  wire comparator_1_lt;
  wire [31:0] add1, and1, divu1, mul1, mulh1, mulhu1, multiplier_1_out, or1, remu1, sll1, slt1, sra1, srl1,
       sub1, xor1;

  Multiplier #(.width(32)) multiplier_1 (.a(B), .b(divu1), .out(multiplier_1_out));  // open: cin, cout
  Comparator #(.width(32)) comparator_1 (.a(A), .b(B), .lt(comparator_1_lt));  // open: gt, eq
  Divider #(.width(32)) divider_1 (.a(A), .b(B), .out(divu1));  // open: upper, rem
  Subtractor #(.width(32)) subtractor_1 (.a(A), .b(multiplier_1_out), .out(remu1));  // open: bin, bout
  Adder #(.width(32)) adder_1 (.a(A), .b(B), .out(add1));  // open: cin, cout
  sll0 sll0_1 (.A(A), .B(B), .Result(sll1));
  mul0 mul0_1 (.A(A), .B(B), .Result(mul1));
  and0 and0_1 (.A(A), .B(B), .Result(and1));
  or0 or0_1 (.A(A), .B(B), .Result(or1));
  xor0 xor0_1 (.A(A), .B(B), .Result(xor1));
  srl0 srl0_1 (.A(A), .B(B), .Result(srl1));
  Multiplexer #(.width(32), .enable("false")) multiplexer_1 (
    .in0({32{1'b0}}), .in1(32'h1), .out(slt1), .sel(comparator_1_lt));
  Subtractor #(.width(32)) subtractor_2 (.a(A), .b(B), .out(sub1));  // open: bin, bout
  sra0 sra0_1 (.A(A), .B(B), .Result(sra1));
  Multiplexer #(.select(4), .width(32), .enable("false")) multiplexer_2 (
    .in0(add1), .in1(and1), .in2(or1), .in3(xor1), .in4(srl1), .in5(sra1), .in6(sll1), .in7(slt1),
    .in8(divu1), .in9(remu1), .in10(mul1), .in11(mulhu1), .in12(sub1), .in13(B), .in14(mulh1), .out(Result),
    .sel(ALUSel));  // open: in15
  mulhu0 mulhu0_1 (.A(A), .B(B), .Result(mulhu1));
  mulh0 mulh0_1 (.A(A), .B(B), .Result(mulh1));

  // Notes on the sheet:
  //   INPUTS to your circuit
  //   DON'T CHANGE THE LOCATIONS OF THE INPUTS AND OUTPUTS!
  //   OUTPUT from your circuit
endmodule

module and0 (
  input  [31:0] A,
  input  [31:0] B,
  output [31:0] Result
);

  and and_1 (Result[0], B[0], A[0]);
  and and_2 (Result[1], B[1], A[1]);
  and and_3 (Result[2], B[2], A[2]);
  and and_4 (Result[3], B[3], A[3]);
  and and_5 (Result[4], B[4], A[4]);
  and and_6 (Result[5], B[5], A[5]);
  and and_7 (Result[6], B[6], A[6]);
  and and_8 (Result[7], B[7], A[7]);
  and and_9 (Result[8], B[8], A[8]);
  and and_10 (Result[9], B[9], A[9]);
  and and_11 (Result[10], B[10], A[10]);
  and and_12 (Result[11], B[11], A[11]);
  and and_13 (Result[12], B[12], A[12]);
  and and_14 (Result[13], B[13], A[13]);
  and and_15 (Result[14], B[14], A[14]);
  and and_16 (Result[15], B[15], A[15]);
  and and_17 (Result[16], B[16], A[16]);
  and and_18 (Result[17], B[17], A[17]);
  and and_19 (Result[18], B[18], A[18]);
  and and_20 (Result[19], B[19], A[19]);
  and and_21 (Result[20], B[20], A[20]);
  and and_22 (Result[21], B[21], A[21]);
  and and_23 (Result[22], B[22], A[22]);
  and and_24 (Result[23], B[23], A[23]);
  and and_25 (Result[24], B[24], A[24]);
  and and_26 (Result[25], B[25], A[25]);
  and and_27 (Result[26], B[26], A[26]);
  and and_28 (Result[27], B[27], A[27]);
  and and_29 (Result[28], B[28], A[28]);
  and and_30 (Result[29], B[29], A[29]);
  and and_31 (Result[30], B[30], A[30]);
  and and_32 (Result[31], B[31], A[31]);
endmodule

module or0 (
  input  [31:0] A,
  input  [31:0] B,
  output [31:0] Result
);

  or or_1 (Result[0], B[0], A[0]);
  or or_2 (Result[1], B[1], A[1]);
  or or_3 (Result[2], B[2], A[2]);
  or or_4 (Result[3], B[3], A[3]);
  or or_5 (Result[4], B[4], A[4]);
  or or_6 (Result[5], B[5], A[5]);
  or or_7 (Result[6], B[6], A[6]);
  or or_8 (Result[7], B[7], A[7]);
  or or_9 (Result[8], B[8], A[8]);
  or or_10 (Result[9], B[9], A[9]);
  or or_11 (Result[10], B[10], A[10]);
  or or_12 (Result[11], B[11], A[11]);
  or or_13 (Result[12], B[12], A[12]);
  or or_14 (Result[13], B[13], A[13]);
  or or_15 (Result[14], B[14], A[14]);
  or or_16 (Result[15], B[15], A[15]);
  or or_17 (Result[16], B[16], A[16]);
  or or_18 (Result[17], B[17], A[17]);
  or or_19 (Result[18], B[18], A[18]);
  or or_20 (Result[19], B[19], A[19]);
  or or_21 (Result[20], B[20], A[20]);
  or or_22 (Result[21], B[21], A[21]);
  or or_23 (Result[22], B[22], A[22]);
  or or_24 (Result[23], B[23], A[23]);
  or or_25 (Result[24], B[24], A[24]);
  or or_26 (Result[25], B[25], A[25]);
  or or_27 (Result[26], B[26], A[26]);
  or or_28 (Result[27], B[27], A[27]);
  or or_29 (Result[28], B[28], A[28]);
  or or_30 (Result[29], B[29], A[29]);
  or or_31 (Result[30], B[30], A[30]);
  or or_32 (Result[31], B[31], A[31]);
endmodule

module xor0 (
  input  [31:0] A,
  input  [31:0] B,
  output [31:0] Result
);

  xor xor_1 (Result[0], B[0], A[0]);
  xor xor_2 (Result[1], B[1], A[1]);
  xor xor_3 (Result[2], B[2], A[2]);
  xor xor_4 (Result[3], B[3], A[3]);
  xor xor_5 (Result[4], B[4], A[4]);
  xor xor_6 (Result[5], B[5], A[5]);
  xor xor_7 (Result[6], B[6], A[6]);
  xor xor_8 (Result[7], B[7], A[7]);
  xor xor_9 (Result[8], B[8], A[8]);
  xor xor_10 (Result[9], B[9], A[9]);
  xor xor_11 (Result[10], B[10], A[10]);
  xor xor_12 (Result[11], B[11], A[11]);
  xor xor_13 (Result[12], B[12], A[12]);
  xor xor_14 (Result[13], B[13], A[13]);
  xor xor_15 (Result[14], B[14], A[14]);
  xor xor_16 (Result[15], B[15], A[15]);
  xor xor_17 (Result[16], B[16], A[16]);
  xor xor_18 (Result[17], B[17], A[17]);
  xor xor_19 (Result[18], B[18], A[18]);
  xor xor_20 (Result[19], B[19], A[19]);
  xor xor_21 (Result[20], B[20], A[20]);
  xor xor_22 (Result[21], B[21], A[21]);
  xor xor_23 (Result[22], B[22], A[22]);
  xor xor_24 (Result[23], B[23], A[23]);
  xor xor_25 (Result[24], B[24], A[24]);
  xor xor_26 (Result[25], B[25], A[25]);
  xor xor_27 (Result[26], B[26], A[26]);
  xor xor_28 (Result[27], B[27], A[27]);
  xor xor_29 (Result[28], B[28], A[28]);
  xor xor_30 (Result[29], B[29], A[29]);
  xor xor_31 (Result[30], B[30], A[30]);
  xor xor_32 (Result[31], B[31], A[31]);
endmodule

module srl0 (
  input  [31:0] A,
  input  [31:0] B,
  output [31:0] Result
);

  wire [4:0] bit_extender_1_out;
  wire [31:0] multiplexer_1_out, multiplexer_2_out, multiplexer_3_out, multiplexer_4_out, shifter_1_out,
       shifter_2_out, shifter_3_out, shifter_4_out, shifter_5_out;

  Bit_Extender #(.in_width(32), .out_width(5)) bit_extender_1 (.in(B), .out(bit_extender_1_out));
  Shifter #(.width(32), .shift("lr")) shifter_1 (.in(A), .\dist (5'b00001), .out(shifter_1_out));
  Multiplexer #(.width(32), .enable("false")) multiplexer_1 (
    .in0(A), .in1(shifter_1_out), .out(multiplexer_1_out), .sel(bit_extender_1_out[0]));
  Multiplexer #(.width(32), .enable("false")) multiplexer_2 (
    .in0(multiplexer_1_out), .in1(shifter_2_out), .out(multiplexer_2_out), .sel(bit_extender_1_out[1]));
  Shifter #(.width(32), .shift("lr")) shifter_2 (.in(multiplexer_1_out), .\dist (5'b00010), .out(shifter_2_out));
  Shifter #(.width(32), .shift("lr")) shifter_3 (.in(multiplexer_2_out), .\dist (5'b00100), .out(shifter_3_out));
  Multiplexer #(.width(32), .enable("false")) multiplexer_3 (
    .in0(multiplexer_2_out), .in1(shifter_3_out), .out(multiplexer_3_out), .sel(bit_extender_1_out[2]));
  Shifter #(.width(32), .shift("lr")) shifter_4 (.in(multiplexer_3_out), .\dist (5'b01000), .out(shifter_4_out));
  Multiplexer #(.width(32), .enable("false")) multiplexer_4 (
    .in0(multiplexer_3_out), .in1(shifter_4_out), .out(multiplexer_4_out), .sel(bit_extender_1_out[3]));
  Multiplexer #(.width(32), .enable("false")) multiplexer_5 (
    .in0(multiplexer_4_out), .in1(shifter_5_out), .out(Result), .sel(bit_extender_1_out[4]));
  Shifter #(.width(32), .shift("lr")) shifter_5 (.in(multiplexer_4_out), .\dist (5'b10000), .out(shifter_5_out));
endmodule

module sra0 (
  input  [31:0] A,
  input  [31:0] B,
  output [31:0] Result
);

  wire [4:0] bit_extender_1_out;
  wire [31:0] multiplexer_1_out, multiplexer_2_out, multiplexer_3_out, multiplexer_4_out, shifter_1_out,
       shifter_2_out, shifter_3_out, shifter_4_out, shifter_5_out;

  Bit_Extender #(.in_width(32), .out_width(5)) bit_extender_1 (.in(B), .out(bit_extender_1_out));
  Shifter #(.width(32), .shift("ar")) shifter_1 (.in(A), .\dist (5'b00001), .out(shifter_1_out));
  Multiplexer #(.width(32), .enable("false")) multiplexer_1 (
    .in0(A), .in1(shifter_1_out), .out(multiplexer_1_out), .sel(bit_extender_1_out[0]));
  Multiplexer #(.width(32), .enable("false")) multiplexer_2 (
    .in0(multiplexer_1_out), .in1(shifter_2_out), .out(multiplexer_2_out), .sel(bit_extender_1_out[1]));
  Shifter #(.width(32), .shift("ar")) shifter_2 (.in(multiplexer_1_out), .\dist (5'b00010), .out(shifter_2_out));
  Shifter #(.width(32), .shift("ar")) shifter_3 (.in(multiplexer_2_out), .\dist (5'b00100), .out(shifter_3_out));
  Multiplexer #(.width(32), .enable("false")) multiplexer_3 (
    .in0(multiplexer_2_out), .in1(shifter_3_out), .out(multiplexer_3_out), .sel(bit_extender_1_out[2]));
  Shifter #(.width(32), .shift("ar")) shifter_4 (.in(multiplexer_3_out), .\dist (5'b01000), .out(shifter_4_out));
  Multiplexer #(.width(32), .enable("false")) multiplexer_4 (
    .in0(multiplexer_3_out), .in1(shifter_4_out), .out(multiplexer_4_out), .sel(bit_extender_1_out[3]));
  Multiplexer #(.width(32), .enable("false")) multiplexer_5 (
    .in0(multiplexer_4_out), .in1(shifter_5_out), .out(Result), .sel(bit_extender_1_out[4]));
  Shifter #(.width(32), .shift("ar")) shifter_5 (.in(multiplexer_4_out), .\dist (5'b10000), .out(shifter_5_out));
endmodule

module sll0 (
  input  [31:0] A,
  input  [31:0] B,
  output [31:0] Result
);

  wire [4:0] bit_extender_1_out;
  wire [31:0] multiplexer_1_out, multiplexer_2_out, multiplexer_3_out, multiplexer_4_out, shifter_1_out,
       shifter_2_out, shifter_3_out, shifter_4_out, shifter_5_out;

  Bit_Extender #(.in_width(32), .out_width(5)) bit_extender_1 (.in(B), .out(bit_extender_1_out));
  Shifter #(.width(32)) shifter_1 (.in(A), .\dist (5'b00001), .out(shifter_1_out));
  Multiplexer #(.width(32), .enable("false")) multiplexer_1 (
    .in0(A), .in1(shifter_1_out), .out(multiplexer_1_out), .sel(bit_extender_1_out[0]));
  Multiplexer #(.width(32), .enable("false")) multiplexer_2 (
    .in0(multiplexer_1_out), .in1(shifter_2_out), .out(multiplexer_2_out), .sel(bit_extender_1_out[1]));
  Shifter #(.width(32)) shifter_2 (.in(multiplexer_1_out), .\dist (5'b00010), .out(shifter_2_out));
  Shifter #(.width(32)) shifter_3 (.in(multiplexer_2_out), .\dist (5'b00100), .out(shifter_3_out));
  Multiplexer #(.width(32), .enable("false")) multiplexer_3 (
    .in0(multiplexer_2_out), .in1(shifter_3_out), .out(multiplexer_3_out), .sel(bit_extender_1_out[2]));
  Shifter #(.width(32)) shifter_4 (.in(multiplexer_3_out), .\dist (5'b01000), .out(shifter_4_out));
  Multiplexer #(.width(32), .enable("false")) multiplexer_4 (
    .in0(multiplexer_3_out), .in1(shifter_4_out), .out(multiplexer_4_out), .sel(bit_extender_1_out[3]));
  Multiplexer #(.width(32), .enable("false")) multiplexer_5 (
    .in0(multiplexer_4_out), .in1(shifter_5_out), .out(Result), .sel(bit_extender_1_out[4]));
  Shifter #(.width(32)) shifter_5 (.in(multiplexer_4_out), .\dist (5'b10000), .out(shifter_5_out));
endmodule

module mulhu0 (
  input  [31:0] A,
  input  [31:0] B,
  output [31:0] Result
);

  wire comparator_1_lt;
  wire [31:0] a_t, ad, adder_1_out, adder_2_out, adder_3_out, adder_4_out, b_t, bc, bit_extender_1_out,
       bit_extender_2_out, c, d, multiplexer_1_out, multiplier_3_out, multiplier_4_out, srl0_1_result,
       srl0_2_result, srl0_3_result;

  Multiplier #(.width(32)) multiplier_1 (.a(b_t), .b(c), .out(bc));  // open: cin, cout
  Multiplier #(.width(32)) multiplier_2 (.a(a_t), .b(d), .out(ad));  // open: cin, cout
  Multiplier #(.width(32)) multiplier_3 (.a(b_t), .b(d), .out(multiplier_3_out));  // open: cin, cout
  assign bit_extender_1_out = {{16{1'b0}}, ad[15:0]};  // Bit_Extender bit_extender_1
  assign bit_extender_2_out = {{16{1'b0}}, bc[15:0]};  // Bit_Extender bit_extender_2
  srl0 srl0_1 (.A(multiplier_3_out), .B(32'h10), .Result(srl0_1_result));
  srl0 srl0_2 (.A(bc), .B(32'h10), .Result(srl0_2_result));
  srl0 srl0_3 (.A(ad), .B(32'h10), .Result(srl0_3_result));
  Adder #(.width(32)) adder_1 (.a(bit_extender_1_out), .b(bit_extender_2_out), .out(adder_1_out));  // open: cin, cout
  assign b_t = {{16{1'b0}}, A[15:0]};  // Bit_Extender bit_extender_3
  assign a_t = {{16{1'b0}}, A[31:16]};  // Bit_Extender bit_extender_4
  assign d = {{16{1'b0}}, B[15:0]};  // Bit_Extender bit_extender_5
  assign c = {{16{1'b0}}, B[31:16]};  // Bit_Extender bit_extender_6
  Multiplier #(.width(32)) multiplier_4 (.a(a_t), .b(c), .out(multiplier_4_out));  // open: cin, cout
  Adder #(.width(32)) adder_2 (.a(srl0_2_result), .b(srl0_3_result), .out(adder_2_out));  // open: cin, cout
  Adder #(.width(32)) adder_3 (.a(srl0_1_result), .b(adder_1_out), .out(adder_3_out));  // open: cin, cout
  Adder #(.width(32)) adder_4 (.a(multiplier_4_out), .b(adder_2_out), .out(adder_4_out));  // open: cin, cout
  Comparator #(.width(32), .mode("unsigned")) comparator_1 (
    .a(32'hffff), .b(adder_3_out), .lt(comparator_1_lt));  // open: gt, eq
  Multiplexer #(.width(32), .enable("false")) multiplexer_1 (
    .in0({32{1'b0}}), .in1(32'h1), .out(multiplexer_1_out), .sel(comparator_1_lt));
  Adder #(.width(32)) adder_5 (.a(adder_4_out), .b(multiplexer_1_out), .out(Result));  // open: cin, cout
endmodule

module mulh0 (
  input  [31:0] A,
  input  [31:0] B,
  output [31:0] Result
);

  wire comparator_1_eq, comparator_2_eq;
  wire [31:0] A0, adder_3_out, adder_4_out, B0, b_t, d, mulhu0_1_result, mulhu0_2_result, multiplier_1_out,
       multiplier_2_out, nn, np, pn, pp, xor0_1_result, xor0_2_result, xor0_3_result, xor0_4_result;

  Multiplier #(.width(32)) multiplier_1 (.a(A0), .b(B), .out(multiplier_1_out));  // open: cin, cout
  Multiplier #(.width(32)) multiplier_2 (.a(A), .b(B0), .out(multiplier_2_out));  // open: cin, cout
  xor0 xor0_1 (.A({32{1'b1}}), .B(A), .Result(xor0_1_result));
  xor0 xor0_2 (.A(B), .B({32{1'b1}}), .Result(xor0_2_result));
  mulhu0 mulhu0_1 (.A(A0), .B(B), .Result(mulhu0_1_result));
  Comparator #(.width(32)) comparator_1 (.a(multiplier_1_out), .b({32{1'b0}}), .eq(comparator_1_eq));  // open: gt, lt
  mulhu0 mulhu0_2 (.A(A), .B(B0), .Result(mulhu0_2_result));
  Comparator #(.width(32)) comparator_2 (.a(multiplier_2_out), .b({32{1'b0}}), .eq(comparator_2_eq));  // open: gt, lt
  Multiplexer #(.select(2), .width(32), .enable("false")) multiplexer_1 (
    .in0(pp), .in1(pn), .in2(np), .in3(nn), .out(Result), .sel({B[31], A[31]}));
  mulhu0 mulhu0_3 (.A(A0), .B(B0), .Result(nn));
  xor0 xor0_3 (.A({32{1'b1}}), .B(mulhu0_1_result), .Result(xor0_3_result));
  Multiplexer #(.width(32), .enable("false")) multiplexer_2 (
    .in0(xor0_3_result), .in1(adder_3_out), .out(pn), .sel(comparator_1_eq));
  xor0 xor0_4 (.A({32{1'b1}}), .B(mulhu0_2_result), .Result(xor0_4_result));
  Multiplexer #(.width(32), .enable("false")) multiplexer_3 (
    .in0(xor0_4_result), .in1(adder_4_out), .out(np), .sel(comparator_2_eq));
  assign b_t = {{1{1'b0}}, A[30:0]};  // Bit_Extender bit_extender_1
  assign d = {{1{1'b0}}, B[30:0]};  // Bit_Extender bit_extender_2
  Adder #(.width(32)) adder_1 (.a(32'h1), .b(xor0_1_result), .out(A0));  // open: cin, cout
  Adder #(.width(32)) adder_2 (.a(xor0_2_result), .b(32'h1), .out(B0));  // open: cin, cout
  Adder #(.width(32)) adder_3 (.a(32'h1), .b(xor0_3_result), .out(adder_3_out));  // open: cin, cout
  Adder #(.width(32)) adder_4 (.a(32'h1), .b(xor0_4_result), .out(adder_4_out));  // open: cin, cout
  mulhu0 mulhu0_4 (.A(b_t), .B(d), .Result(pp));

  // Other names for the same wires on the sheet: a0_t[31:0] = A; a_t = A[31]; b0_t[31:0] = B; c = B[31]
endmodule

module mul0 (
  input  [31:0] A,
  input  [31:0] B,
  output [31:0] Result
);

  wire [31:0] A0, B0, b_t, d, multiplier_2_out, multiplier_3_out, nn, np, pn, pp, xor0_1_result,
       xor0_2_result, xor0_3_result, xor0_4_result;

  xor0 xor0_1 (.A({32{1'b1}}), .B(A), .Result(xor0_1_result));
  xor0 xor0_2 (.A(B), .B({32{1'b1}}), .Result(xor0_2_result));
  Multiplier #(.width(32)) multiplier_1 (.a(A0), .b(B0), .out(nn));  // open: cin, cout
  Multiplier #(.width(32)) multiplier_2 (.a(A0), .b(B), .out(multiplier_2_out));  // open: cin, cout
  Multiplier #(.width(32)) multiplier_3 (.a(A), .b(B0), .out(multiplier_3_out));  // open: cin, cout
  Multiplexer #(.select(2), .width(32), .enable("false")) multiplexer_1 (
    .in0(pp), .in1(pn), .in2(np), .in3(nn), .out(Result), .sel({B[31], A[31]}));
  assign b_t = {{1{1'b0}}, A[30:0]};  // Bit_Extender bit_extender_1
  assign d = {{1{1'b0}}, B[30:0]};  // Bit_Extender bit_extender_2
  Adder #(.width(32)) adder_1 (.a(32'h1), .b(xor0_1_result), .out(A0));  // open: cin, cout
  Adder #(.width(32)) adder_2 (.a(xor0_2_result), .b(32'h1), .out(B0));  // open: cin, cout
  xor0 xor0_3 (.A({32{1'b1}}), .B(multiplier_2_out), .Result(xor0_3_result));
  xor0 xor0_4 (.A({32{1'b1}}), .B(multiplier_3_out), .Result(xor0_4_result));
  Multiplier #(.width(32)) multiplier_4 (.a(B), .b(A), .out(pp));  // open: cin, cout
  Adder #(.width(32)) adder_3 (.a(32'h1), .b(xor0_3_result), .out(pn));  // open: cin, cout
  Adder #(.width(32)) adder_4 (.a(32'h1), .b(xor0_4_result), .out(np));  // open: cin, cout

  // Other names for the same wires on the sheet: a0_t[31:0] = A; a_t = A[31]; b0_t[31:0] = B; c = B[31]
endmodule
