// Logisim project imm_gen.circ as structural Verilog: 1 circuit, main circuit imm_gen
module imm_gen (
  input  [31:0] inst,
  input  [2:0] ImmSel,
  output [31:0] imm
);

  wire [31:0] R;
  wire [31:11] I, S;
  wire [31:12] SB;

  assign R = {{20{inst[31]}}, inst[31:20]};  // Bit_Extender bit_extender_1
  assign I = {{20{inst[31]}}, inst[31]};  // Bit_Extender bit_extender_2
  assign S = {{20{inst[31]}}, inst[31]};  // Bit_Extender bit_extender_3
  assign SB = {{19{inst[31]}}, inst[31]};  // Bit_Extender bit_extender_4
  Multiplexer #(.select(3), .width(32), .enable("false")) multiplexer_1 (
    .in0(R), .in1({I, inst[30:20]}), .in2({S, inst[30:25], inst[11:7]}),
    .in3({SB, inst[7], inst[30:25], inst[11:8], 1'b0}), .in4({inst[31:12], {12{1'b0}}}),
    .in5({inst[31:12], {12{1'b0}}}), .out(imm), .sel(ImmSel));  // open: in6, in7

  // Other names for the same wires on the sheet: S[10:0] = {inst[30:25], inst[11:7]};
  //   SB[11:1] = {inst[7], inst[30:25], inst[11:8]}; U[31:12] = inst[31:12]; UJ[31:12] = inst[31:12];
  //   I[10:0] = inst[30:20]

  // Notes on the sheet:
  //   INPUTS to your circuit
  //   DON'T CHANGE THE LOCATIONS OF THE INPUTS AND OUTPUTS!
  //   OUTPUT from your circuit
endmodule
