// Logisim project alu.circ as structural Verilog: 7 circuits, main circuit alu
module alu (
  input  [31:0] A,
  input  [31:0] B,
  input  [3:0] ALUSel,
  output [31:0] Result
);

  wire comparator_1_lt;
  wire [31:0] add1, and1, divu1, mul1, mulh1, mulhu1, multiplier_1_out, or1, remu1, sll1, slt1, sra1, srl1,
       sub1, xor1;

  Multiplier #(.width(32)) multiplier_1 (.a(B), .b(divu1), .out(multiplier_1_out));  // open: cin, cout
  Comparator #(.width(32)) comparator_1 (.a(A), .b(B), .lt(comparator_1_lt));  // open: gt, eq
  Divider #(.width(32)) divider_1 (.a(A), .b(B), .out(divu1));  // open: upper, rem
  Subtractor #(.width(32)) subtractor_1 (.a(A), .b(multiplier_1_out), .out(remu1));  // open: bin, bout
  Adder #(.width(32)) adder_1 (.a(A), .b(B), .out(add1));  // open: cin, cout
  assign and1 = A & B;  // AND_Gate and_1, 32 bits wide
  assign or1 = A | B;  // OR_Gate or_1, 32 bits wide
  assign xor1 = A ^ B;  // XOR_Gate xor_1, 32 bits wide
  sll0 sll0_1 (.A(A), .B(B), .Result(sll1));
  mul0 mul0_1 (.A(A), .B(B), .Result(mul1));
  srl0 srl0_1 (.A(A), .B(B), .Result(srl1));
  Multiplexer #(.width(32), .enable("false")) multiplexer_1 (
    .in0({32{1'b0}}), .in1(32'h1), .out(slt1), .sel(comparator_1_lt));
  Subtractor #(.width(32)) subtractor_2 (.a(A), .b(B), .out(sub1));  // open: bin, bout
  sra0 sra0_1 (.A(A), .B(B), .Result(sra1));
  Multiplexer #(.select(4), .width(32), .enable("false")) multiplexer_2 (
    .in0(add1), .in1(and1), .in2(or1), .in3(xor1), .in4(srl1), .in5(sra1), .in6(sll1), .in7(slt1),
    .in8(divu1), .in9(remu1), .in10(mul1), .in11(mulhu1), .in12(sub1), .in13(B), .in14(mulh1), .out(Result),
    .sel(ALUSel));  // open: in15
  mulhu0 mulhu0_1 (.A(A), .B(B), .Result(mulhu1));
  mulh0 mulh0_1 (.A(A), .B(B), .Result(mulh1));

  // Notes on the sheet:
  //   INPUTS to your circuit
  //   DON'T CHANGE THE LOCATIONS OF THE INPUTS AND OUTPUTS!
  //   OUTPUT from your circuit
endmodule

module srl0 (
  input  [31:0] A,
  input  [31:0] B,
  output [31:0] Result
);

  wire [4:0] bit_extender_1_out;
  wire [31:0] multiplexer_1_out, multiplexer_2_out, multiplexer_3_out, multiplexer_4_out, shifter_1_out,
       shifter_2_out, shifter_3_out, shifter_4_out, shifter_5_out;

  Bit_Extender #(.in_width(32), .out_width(5)) bit_extender_1 (.in(B), .out(bit_extender_1_out));
  Shifter #(.width(32), .shift("lr")) shifter_1 (.in(A), .\dist (5'b00001), .out(shifter_1_out));
  Multiplexer #(.width(32), .enable("false")) multiplexer_1 (
    .in0(A), .in1(shifter_1_out), .out(multiplexer_1_out), .sel(bit_extender_1_out[0]));
  Multiplexer #(.width(32), .enable("false")) multiplexer_2 (
    .in0(multiplexer_1_out), .in1(shifter_2_out), .out(multiplexer_2_out), .sel(bit_extender_1_out[1]));
  Shifter #(.width(32), .shift("lr")) shifter_2 (.in(multiplexer_1_out), .\dist (5'b00010), .out(shifter_2_out));
  Shifter #(.width(32), .shift("lr")) shifter_3 (.in(multiplexer_2_out), .\dist (5'b00100), .out(shifter_3_out));
  Multiplexer #(.width(32), .enable("false")) multiplexer_3 (
    .in0(multiplexer_2_out), .in1(shifter_3_out), .out(multiplexer_3_out), .sel(bit_extender_1_out[2]));
  Shifter #(.width(32), .shift("lr")) shifter_4 (.in(multiplexer_3_out), .\dist (5'b01000), .out(shifter_4_out));
  Multiplexer #(.width(32), .enable("false")) multiplexer_4 (
    .in0(multiplexer_3_out), .in1(shifter_4_out), .out(multiplexer_4_out), .sel(bit_extender_1_out[3]));
  Multiplexer #(.width(32), .enable("false")) multiplexer_5 (
    .in0(multiplexer_4_out), .in1(shifter_5_out), .out(Result), .sel(bit_extender_1_out[4]));
  Shifter #(.width(32), .shift("lr")) shifter_5 (.in(multiplexer_4_out), .\dist (5'b10000), .out(shifter_5_out));
endmodule

module sra0 (
  input  [31:0] A,
  input  [31:0] B,
  output [31:0] Result
);

  wire [4:0] bit_extender_1_out;
  wire [31:0] multiplexer_1_out, multiplexer_2_out, multiplexer_3_out, multiplexer_4_out, shifter_1_out,
       shifter_2_out, shifter_3_out, shifter_4_out, shifter_5_out;

  Bit_Extender #(.in_width(32), .out_width(5)) bit_extender_1 (.in(B), .out(bit_extender_1_out));
  Shifter #(.width(32), .shift("ar")) shifter_1 (.in(A), .\dist (5'b00001), .out(shifter_1_out));
  Multiplexer #(.width(32), .enable("false")) multiplexer_1 (
    .in0(A), .in1(shifter_1_out), .out(multiplexer_1_out), .sel(bit_extender_1_out[0]));
  Multiplexer #(.width(32), .enable("false")) multiplexer_2 (
    .in0(multiplexer_1_out), .in1(shifter_2_out), .out(multiplexer_2_out), .sel(bit_extender_1_out[1]));
  Shifter #(.width(32), .shift("ar")) shifter_2 (.in(multiplexer_1_out), .\dist (5'b00010), .out(shifter_2_out));
  Shifter #(.width(32), .shift("ar")) shifter_3 (.in(multiplexer_2_out), .\dist (5'b00100), .out(shifter_3_out));
  Multiplexer #(.width(32), .enable("false")) multiplexer_3 (
    .in0(multiplexer_2_out), .in1(shifter_3_out), .out(multiplexer_3_out), .sel(bit_extender_1_out[2]));
  Shifter #(.width(32), .shift("ar")) shifter_4 (.in(multiplexer_3_out), .\dist (5'b01000), .out(shifter_4_out));
  Multiplexer #(.width(32), .enable("false")) multiplexer_4 (
    .in0(multiplexer_3_out), .in1(shifter_4_out), .out(multiplexer_4_out), .sel(bit_extender_1_out[3]));
  Multiplexer #(.width(32), .enable("false")) multiplexer_5 (
    .in0(multiplexer_4_out), .in1(shifter_5_out), .out(Result), .sel(bit_extender_1_out[4]));
  Shifter #(.width(32), .shift("ar")) shifter_5 (.in(multiplexer_4_out), .\dist (5'b10000), .out(shifter_5_out));
endmodule

module sll0 (
  input  [31:0] A,
  input  [31:0] B,
  output [31:0] Result
);

  wire [4:0] bit_extender_1_out;
  wire [31:0] multiplexer_1_out, multiplexer_2_out, multiplexer_3_out, multiplexer_4_out, shifter_1_out,
       shifter_2_out, shifter_3_out, shifter_4_out, shifter_5_out;

  Bit_Extender #(.in_width(32), .out_width(5)) bit_extender_1 (.in(B), .out(bit_extender_1_out));
  Shifter #(.width(32)) shifter_1 (.in(A), .\dist (5'b00001), .out(shifter_1_out));
  Multiplexer #(.width(32), .enable("false")) multiplexer_1 (
    .in0(A), .in1(shifter_1_out), .out(multiplexer_1_out), .sel(bit_extender_1_out[0]));
  Multiplexer #(.width(32), .enable("false")) multiplexer_2 (
    .in0(multiplexer_1_out), .in1(shifter_2_out), .out(multiplexer_2_out), .sel(bit_extender_1_out[1]));
  Shifter #(.width(32)) shifter_2 (.in(multiplexer_1_out), .\dist (5'b00010), .out(shifter_2_out));
  Shifter #(.width(32)) shifter_3 (.in(multiplexer_2_out), .\dist (5'b00100), .out(shifter_3_out));
  Multiplexer #(.width(32), .enable("false")) multiplexer_3 (
    .in0(multiplexer_2_out), .in1(shifter_3_out), .out(multiplexer_3_out), .sel(bit_extender_1_out[2]));
  Shifter #(.width(32)) shifter_4 (.in(multiplexer_3_out), .\dist (5'b01000), .out(shifter_4_out));
  Multiplexer #(.width(32), .enable("false")) multiplexer_4 (
    .in0(multiplexer_3_out), .in1(shifter_4_out), .out(multiplexer_4_out), .sel(bit_extender_1_out[3]));
  Multiplexer #(.width(32), .enable("false")) multiplexer_5 (
    .in0(multiplexer_4_out), .in1(shifter_5_out), .out(Result), .sel(bit_extender_1_out[4]));
  Shifter #(.width(32)) shifter_5 (.in(multiplexer_4_out), .\dist (5'b10000), .out(shifter_5_out));
endmodule

module mulhu0 (
  input  [31:0] A,
  input  [31:0] B,
  output [31:0] Result
);

  wire comparator_1_lt;
  wire [31:0] a_t, ad, adder_1_out, adder_2_out, adder_3_out, adder_4_out, b_t, bc, bit_extender_1_out,
       bit_extender_2_out, c, d, multiplexer_1_out, multiplier_3_out, multiplier_4_out, srl0_1_result,
       srl0_2_result, srl0_3_result;

  Multiplier #(.width(32)) multiplier_1 (.a(b_t), .b(c), .out(bc));  // open: cin, cout
  Multiplier #(.width(32)) multiplier_2 (.a(a_t), .b(d), .out(ad));  // open: cin, cout
  Multiplier #(.width(32)) multiplier_3 (.a(b_t), .b(d), .out(multiplier_3_out));  // open: cin, cout
  assign bit_extender_1_out = {{16{1'b0}}, ad[15:0]};  // Bit_Extender bit_extender_1
  assign bit_extender_2_out = {{16{1'b0}}, bc[15:0]};  // Bit_Extender bit_extender_2
  srl0 srl0_1 (.A(multiplier_3_out), .B(32'h10), .Result(srl0_1_result));
  srl0 srl0_2 (.A(bc), .B(32'h10), .Result(srl0_2_result));
  srl0 srl0_3 (.A(ad), .B(32'h10), .Result(srl0_3_result));
  Adder #(.width(32)) adder_1 (.a(bit_extender_1_out), .b(bit_extender_2_out), .out(adder_1_out));  // open: cin, cout
  assign b_t = {{16{1'b0}}, A[15:0]};  // Bit_Extender bit_extender_3
  assign a_t = {{16{1'b0}}, A[31:16]};  // Bit_Extender bit_extender_4
  assign d = {{16{1'b0}}, B[15:0]};  // Bit_Extender bit_extender_5
  assign c = {{16{1'b0}}, B[31:16]};  // Bit_Extender bit_extender_6
  Multiplier #(.width(32)) multiplier_4 (.a(a_t), .b(c), .out(multiplier_4_out));  // open: cin, cout
  Adder #(.width(32)) adder_2 (.a(srl0_2_result), .b(srl0_3_result), .out(adder_2_out));  // open: cin, cout
  Adder #(.width(32)) adder_3 (.a(srl0_1_result), .b(adder_1_out), .out(adder_3_out));  // open: cin, cout
  Adder #(.width(32)) adder_4 (.a(multiplier_4_out), .b(adder_2_out), .out(adder_4_out));  // open: cin, cout
  Comparator #(.width(32), .mode("unsigned")) comparator_1 (
    .a(32'hffff), .b(adder_3_out), .lt(comparator_1_lt));  // open: gt, eq
  Multiplexer #(.width(32), .enable("false")) multiplexer_1 (
    .in0({32{1'b0}}), .in1(32'h1), .out(multiplexer_1_out), .sel(comparator_1_lt));
  Adder #(.width(32)) adder_5 (.a(adder_4_out), .b(multiplexer_1_out), .out(Result));  // open: cin, cout
endmodule

module mulh0 (
  input  [31:0] A,
  input  [31:0] B,
  output [31:0] Result
);

  wire comparator_1_eq, comparator_2_eq;
  wire [31:0] A0, adder_3_out, adder_4_out, B0, b_t, d, mulhu0_1_result, mulhu0_2_result, multiplier_1_out,
       multiplier_2_out, nn, np, pn, pp, xor_1_out, xor_2_out, xor_3_out, xor_4_out;

  Multiplier #(.width(32)) multiplier_1 (.a(A0), .b(B), .out(multiplier_1_out));  // open: cin, cout
  Multiplier #(.width(32)) multiplier_2 (.a(A), .b(B0), .out(multiplier_2_out));  // open: cin, cout
  assign xor_1_out = {32{1'b1}} ^ A;  // XOR_Gate xor_1, 32 bits wide
  assign xor_2_out = B ^ {32{1'b1}};  // XOR_Gate xor_2, 32 bits wide
  mulhu0 mulhu0_1 (.A(A0), .B(B), .Result(mulhu0_1_result));
  Comparator #(.width(32)) comparator_1 (.a(multiplier_1_out), .b({32{1'b0}}), .eq(comparator_1_eq));  // open: gt, lt
  mulhu0 mulhu0_2 (.A(A), .B(B0), .Result(mulhu0_2_result));
  Comparator #(.width(32)) comparator_2 (.a(multiplier_2_out), .b({32{1'b0}}), .eq(comparator_2_eq));  // open: gt, lt
  Multiplexer #(.select(2), .width(32), .enable("false")) multiplexer_1 (
    .in0(pp), .in1(pn), .in2(np), .in3(nn), .out(Result), .sel({B[31], A[31]}));
  mulhu0 mulhu0_3 (.A(A0), .B(B0), .Result(nn));
  assign xor_3_out = {32{1'b1}} ^ mulhu0_1_result;  // XOR_Gate xor_3, 32 bits wide
  Multiplexer #(.width(32), .enable("false")) multiplexer_2 (
    .in0(xor_3_out), .in1(adder_3_out), .out(pn), .sel(comparator_1_eq));
  assign xor_4_out = {32{1'b1}} ^ mulhu0_2_result;  // XOR_Gate xor_4, 32 bits wide
  Multiplexer #(.width(32), .enable("false")) multiplexer_3 (
    .in0(xor_4_out), .in1(adder_4_out), .out(np), .sel(comparator_2_eq));
  assign b_t = {{1{1'b0}}, A[30:0]};  // Bit_Extender bit_extender_1
  assign d = {{1{1'b0}}, B[30:0]};  // Bit_Extender bit_extender_2
  Adder #(.width(32)) adder_1 (.a(32'h1), .b(xor_1_out), .out(A0));  // open: cin, cout
  Adder #(.width(32)) adder_2 (.a(xor_2_out), .b(32'h1), .out(B0));  // open: cin, cout
  Adder #(.width(32)) adder_3 (.a(32'h1), .b(xor_3_out), .out(adder_3_out));  // open: cin, cout
  Adder #(.width(32)) adder_4 (.a(32'h1), .b(xor_4_out), .out(adder_4_out));  // open: cin, cout
  mulhu0 mulhu0_4 (.A(b_t), .B(d), .Result(pp));

  // Other names for the same wires on the sheet: a0_t[31:0] = A; a_t = A[31]; b0_t[31:0] = B; c = B[31]
endmodule

module mul0 (
  input  [31:0] A,
  input  [31:0] B,
  output [31:0] Result
);

  wire [31:0] A0, B0, b_t, d, multiplier_2_out, multiplier_3_out, nn, np, pn, pp, xor_1_out, xor_2_out,
       xor_3_out, xor_4_out;

  assign xor_1_out = {32{1'b1}} ^ A;  // XOR_Gate xor_1, 32 bits wide
  assign xor_2_out = B ^ {32{1'b1}};  // XOR_Gate xor_2, 32 bits wide
  Multiplier #(.width(32)) multiplier_1 (.a(A0), .b(B0), .out(nn));  // open: cin, cout
  Multiplier #(.width(32)) multiplier_2 (.a(A0), .b(B), .out(multiplier_2_out));  // open: cin, cout
  Multiplier #(.width(32)) multiplier_3 (.a(A), .b(B0), .out(multiplier_3_out));  // open: cin, cout
  Multiplexer #(.select(2), .width(32), .enable("false")) multiplexer_1 (
    .in0(pp), .in1(pn), .in2(np), .in3(nn), .out(Result), .sel({B[31], A[31]}));
  assign b_t = {{1{1'b0}}, A[30:0]};  // Bit_Extender bit_extender_1
  assign d = {{1{1'b0}}, B[30:0]};  // Bit_Extender bit_extender_2
  Adder #(.width(32)) adder_1 (.a(32'h1), .b(xor_1_out), .out(A0));  // open: cin, cout
  Adder #(.width(32)) adder_2 (.a(xor_2_out), .b(32'h1), .out(B0));  // open: cin, cout
  assign xor_3_out = {32{1'b1}} ^ multiplier_2_out;  // XOR_Gate xor_3, 32 bits wide
  assign xor_4_out = {32{1'b1}} ^ multiplier_3_out;  // XOR_Gate xor_4, 32 bits wide
  Multiplier #(.width(32)) multiplier_4 (.a(B), .b(A), .out(pp));  // open: cin, cout
  Adder #(.width(32)) adder_3 (.a(32'h1), .b(xor_3_out), .out(pn));  // open: cin, cout
  Adder #(.width(32)) adder_4 (.a(32'h1), .b(xor_4_out), .out(np));  // open: cin, cout

  // Other names for the same wires on the sheet: a0_t[31:0] = A; a_t = A[31]; b0_t[31:0] = B; c = B[31]
endmodule
