// Logisim project branch_comp.circ as structural Verilog: 1 circuit, main circuit branch_comp
module branch_comp (
  input  [31:0] rs1,
  input  [31:0] rs2,
  input  BrUn,
  output BrEq,
  output BrLt
);

  wire and_1_out, and_2_out, comparator_1_lt, comparator_2_lt, not_1_out;

  Comparator #(.width(32), .mode("unsigned")) comparator_1 (
    .a(rs1), .b(rs2), .eq(BrEq), .lt(comparator_1_lt));  // open: gt
  Comparator #(.width(32), .mode("unsigned")) comparator_2 (.a(rs1), .b(rs2), .lt(comparator_2_lt));  // open: gt, eq
  not not_1 (not_1_out, BrUn);
  and and_1 (and_1_out, comparator_1_lt, BrUn);
  and and_2 (and_2_out, comparator_2_lt, not_1_out);
  or or_1 (BrLt, and_1_out, and_2_out);

  // Notes on the sheet:
  //   INPUTS to your circuit
  //   DON'T CHANGE THE LOCATIONS OF THE INPUTS AND OUTPUTS!
  //   OUTPUT from your circuit
endmodule
