// Logisim project control_logic.circ as structural Verilog: 1 circuit, main circuit control_logic
module control_logic (
  input  [31:0] inst,
  input  BrEq,
  input  BrLt,
  output PCSel,
  output RegWEn,
  output [2:0] ImmSel,
  output BrUn,
  output ASel,
  output BSel,
  output [3:0] ALUSel,
  output MemRW,
  output [1:0] WBSel,
  output [3:0] out_13,
  output [4:0] out_14,
  output [2:0] out_15
);

  wire ALUB, and_1_out, and_2_out, and_3_out, and_4_out, and_5_out, and_6_out, and_7_out, and_8_out,
       and_9_out, and_10_out, and_11_out, and_44_out, and_45_out, and_46_out, and_47_out, and_48_out,
       and_49_out, and_50_out, comparator_2_eq, comparator_3_eq, comparator_4_eq, comparator_5_eq,
       comparator_6_eq, comparator_7_eq, comparator_8_eq, comparator_9_eq, comparator_10_eq,
       comparator_11_eq, comparator_12_eq, comparator_13_eq, comparator_14_eq, comparator_15_eq,
       comparator_16_eq, comparator_17_eq, comparator_18_eq, comparator_19_eq, comparator_20_eq,
       comparator_21_eq, comparator_22_eq, comparator_23_eq, comparator_24_eq, comparator_25_eq,
       comparator_26_eq, comparator_27_eq, comparator_28_eq, comparator_29_eq, comparator_30_eq,
       comparator_31_eq, comparator_33_eq, comparator_34_eq, comparator_35_eq, comparator_36_eq,
       comparator_37_eq, comparator_38_eq, comparator_39_eq, comparator_40_eq, comparator_41_eq,
       comparator_42_eq, comparator_43_eq, comparator_44_eq, comparator_45_eq, comparator_46_eq,
       comparator_47_eq, comparator_48_eq, comparator_49_eq, comparator_50_eq, comparator_51_eq,
       comparator_52_eq, comparator_53_eq, comparator_54_eq, comparator_55_eq, comparator_56_eq,
       comparator_57_eq, comparator_58_eq, comparator_59_eq, comparator_60_eq, comparator_61_eq,
       comparator_62_eq, comparator_63_eq, comparator_64_eq, comparator_65_eq, comparator_66_eq,
       comparator_67_eq, comparator_68_eq, comparator_69_eq, comparator_70_eq, comparator_71_eq,
       comparator_72_eq, comparator_73_eq, comparator_74_eq, comparator_75_eq, jal_jalr_sel, not_1_out,
       not_2_out, not_3_out, or_4_out, or_12_out;
  wire [1:0] and_21_out, and_24_out, and_25_out, and_26_out, and_27_out, bit_extender_11_out,
       bit_extender_13_out, bit_extender_14_out, bit_extender_15_out, bit_extender_16_out;
  wire [2:0] and_12_out, and_13_out, and_14_out, and_15_out, and_16_out, and_17_out, and_18_out, and_19_out,
       and_20_out, and_22_out, bit_extender_1_out, bit_extender_2_out, bit_extender_3_out,
       bit_extender_4_out, bit_extender_5_out, bit_extender_6_out, bit_extender_7_out, bit_extender_8_out,
       bit_extender_9_out, bit_extender_10_out;
  wire [3:0] ALUSelI, ALUSelR, and_23_out, and_28_out, and_29_out, and_30_out, and_31_out, and_32_out,
       and_33_out, and_34_out, and_35_out, and_36_out, and_37_out, and_38_out, and_39_out, and_40_out,
       and_41_out, and_42_out, and_43_out, and_51_out, and_52_out, and_53_out, and_54_out, and_55_out,
       and_56_out, and_57_out, and_58_out, bit_extender_12_out, bit_extender_17_out, bit_extender_18_out,
       bit_extender_19_out, bit_extender_20_out, bit_extender_21_out, bit_extender_22_out,
       bit_extender_23_out, bit_extender_24_out, bit_extender_25_out, bit_extender_26_out,
       bit_extender_27_out, bit_extender_28_out, bit_extender_29_out, bit_extender_30_out,
       bit_extender_31_out, bit_extender_32_out, bit_extender_33_out, bit_extender_34_out,
       bit_extender_35_out, bit_extender_36_out, bit_extender_37_out, bit_extender_38_out,
       bit_extender_39_out, bit_extender_40_out;

  Comparator #(.width(7)) comparator_1 (.a(inst[6:0]), .b(7'b0100011), .eq(MemRW));  // open: gt, lt
  Comparator #(.width(7)) comparator_2 (.a(inst[6:0]), .b(7'b0110011), .eq(comparator_2_eq));  // open: gt, lt
  Comparator #(.width(7)) comparator_3 (.a(inst[6:0]), .b(7'b0010011), .eq(comparator_3_eq));  // open: gt, lt
  Comparator #(.width(7)) comparator_4 (.a(inst[6:0]), .b(7'b0000011), .eq(comparator_4_eq));  // open: gt, lt
  Comparator #(.width(7)) comparator_5 (.a(inst[6:0]), .b(7'b0100011), .eq(comparator_5_eq));  // open: gt, lt
  Comparator #(.width(7)) comparator_6 (.a(inst[6:0]), .b(7'b0110011), .eq(comparator_6_eq));  // open: gt, lt
  Comparator #(.width(7)) comparator_7 (.a(inst[6:0]), .b(7'b0000011), .eq(comparator_7_eq));  // open: gt, lt
  Comparator #(.width(7)) comparator_8 (.a(inst[6:0]), .b(7'b0010011), .eq(comparator_8_eq));  // open: gt, lt
  Comparator #(.width(7)) comparator_9 (.a(inst[6:0]), .b(7'b0100011), .eq(comparator_9_eq));  // open: gt, lt
  Comparator #(.width(7)) comparator_10 (.a(inst[6:0]), .b(7'b1100011), .eq(comparator_10_eq));  // open: gt, lt
  Comparator #(.width(7)) comparator_11 (.a(inst[6:0]), .b(7'b0010111), .eq(comparator_11_eq));  // open: gt, lt
  Comparator #(.width(7)) comparator_12 (.a(inst[6:0]), .b(7'b0110111), .eq(comparator_12_eq));  // open: gt, lt
  Comparator #(.width(7)) comparator_13 (.a(inst[6:0]), .b(7'b1101111), .eq(comparator_13_eq));  // open: gt, lt
  Comparator #(.width(7)) comparator_14 (.a(inst[6:0]), .b(7'b1100111), .eq(comparator_14_eq));  // open: gt, lt
  Comparator #(.width(7)) comparator_15 (.a(inst[6:0]), .b(7'b0110011), .eq(comparator_15_eq));  // open: gt, lt
  Comparator #(.width(7)) comparator_16 (.a(inst[6:0]), .b(7'b0010011), .eq(comparator_16_eq));  // open: gt, lt
  Comparator #(.width(7)) comparator_17 (.a(inst[6:0]), .b(7'b0000011), .eq(comparator_17_eq));  // open: gt, lt
  Comparator #(.width(7)) comparator_18 (.a(inst[6:0]), .b(7'b0110111), .eq(comparator_18_eq));  // open: gt, lt
  Comparator #(.width(7)) comparator_19 (.a(inst[6:0]), .b(7'b0010111), .eq(comparator_19_eq));  // open: gt, lt
  Comparator #(.width(7)) comparator_20 (.a(inst[6:0]), .b(7'b1101111), .eq(comparator_20_eq));  // open: gt, lt
  Comparator #(.width(7)) comparator_21 (.a(inst[6:0]), .b(7'b1100111), .eq(comparator_21_eq));  // open: gt, lt
  assign bit_extender_1_out = {{2{comparator_6_eq}}, comparator_6_eq};  // Bit_Extender bit_extender_1
  assign bit_extender_2_out = {{2{comparator_7_eq}}, comparator_7_eq};  // Bit_Extender bit_extender_2
  assign bit_extender_3_out = {{2{comparator_8_eq}}, comparator_8_eq};  // Bit_Extender bit_extender_3
  assign bit_extender_4_out = {{2{comparator_9_eq}}, comparator_9_eq};  // Bit_Extender bit_extender_4
  assign bit_extender_5_out = {{2{comparator_10_eq}}, comparator_10_eq};  // Bit_Extender bit_extender_5
  assign bit_extender_6_out = {{2{comparator_11_eq}}, comparator_11_eq};  // Bit_Extender bit_extender_6
  assign bit_extender_7_out = {{2{comparator_12_eq}}, comparator_12_eq};  // Bit_Extender bit_extender_7
  assign bit_extender_8_out = {{2{comparator_13_eq}}, comparator_13_eq};  // Bit_Extender bit_extender_8
  assign bit_extender_9_out = {{2{comparator_14_eq}}, comparator_14_eq};  // Bit_Extender bit_extender_9
  and and_1 (and_1_out, comparator_15_eq, 1'b1);
  and and_2 (and_2_out, comparator_16_eq, 1'b1);
  and and_3 (and_3_out, comparator_17_eq, 1'b1);
  and and_4 (and_4_out, comparator_18_eq, 1'b1);
  and and_5 (and_5_out, comparator_19_eq, 1'b1);
  and and_6 (and_6_out, comparator_20_eq, 1'b1);
  and and_7 (and_7_out, comparator_21_eq, 1'b1);
  and and_8 (and_8_out, comparator_2_eq, 1'b1);
  and and_9 (and_9_out, comparator_3_eq, 1'b1);
  and and_10 (and_10_out, comparator_4_eq, 1'b1);
  and and_11 (and_11_out, comparator_5_eq, 1'b1);
  assign and_12_out = bit_extender_1_out & 3'b000;  // AND_Gate and_12, 3 bits wide
  assign and_13_out = bit_extender_2_out & 3'b001;  // AND_Gate and_13, 3 bits wide
  assign and_14_out = bit_extender_3_out & 3'b001;  // AND_Gate and_14, 3 bits wide
  assign and_15_out = bit_extender_4_out & 3'b010;  // AND_Gate and_15, 3 bits wide
  assign and_16_out = bit_extender_5_out & 3'b011;  // AND_Gate and_16, 3 bits wide
  assign and_17_out = bit_extender_6_out & 3'b100;  // AND_Gate and_17, 3 bits wide
  assign and_18_out = bit_extender_7_out & 3'b100;  // AND_Gate and_18, 3 bits wide
  assign and_19_out = bit_extender_8_out & 3'b101;  // AND_Gate and_19, 3 bits wide
  assign and_20_out = bit_extender_9_out & 3'b001;  // AND_Gate and_20, 3 bits wide
  or or_1 (ALUB, and_8_out, and_9_out, and_10_out, and_11_out);
  or or_2 (RegWEn, and_1_out, and_2_out, and_3_out, and_4_out, and_5_out, and_6_out, and_7_out, 1'b0);
  Comparator #(.width(7)) comparator_22 (.a(inst[6:0]), .b(7'b0110111), .eq(comparator_22_eq));  // open: gt, lt
  assign ImmSel = and_12_out | and_13_out | and_14_out | and_15_out | and_16_out | and_17_out | and_18_out | and_19_out | and_20_out;  // OR_Gate or_3, 3 bits wide
  assign bit_extender_10_out = {{2{comparator_23_eq}}, comparator_23_eq};  // Bit_Extender bit_extender_10
  Comparator #(.width(7)) comparator_23 (.a(inst[6:0]), .b(7'b0100011), .eq(comparator_23_eq));  // open: gt, lt
  assign bit_extender_11_out = {{1{comparator_22_eq}}, comparator_22_eq};  // Bit_Extender bit_extender_11
  assign and_21_out = bit_extender_11_out & 2'b01;  // AND_Gate and_21, 2 bits wide
  Comparator #(.width(7)) comparator_24 (.a(inst[6:0]), .b(7'b1101111), .eq(comparator_24_eq));  // open: gt, lt
  Comparator #(.width(7)) comparator_25 (.a(inst[6:0]), .b(7'b0010111), .eq(comparator_25_eq));  // open: gt, lt
  Comparator #(.width(7)) comparator_26 (.a(inst[6:0]), .b(7'b1100011), .eq(comparator_26_eq));  // open: gt, lt
  assign and_22_out = bit_extender_10_out & inst[14:12];  // AND_Gate and_22, 3 bits wide
  Comparator #(.width(7)) comparator_27 (.a(inst[6:0]), .b(7'b0010111), .eq(comparator_27_eq));  // open: gt, lt
  Comparator #(.width(7)) comparator_28 (.a(inst[6:0]), .b(7'b0110111), .eq(comparator_28_eq));  // open: gt, lt
  Comparator #(.width(7)) comparator_29 (.a(inst[6:0]), .b(7'b0110111), .eq(comparator_29_eq));  // open: gt, lt
  Comparator #(.width(3)) comparator_30 (.a(inst[14:12]), .b(3'b111), .eq(comparator_30_eq));  // open: gt, lt
  Comparator #(.width(3)) comparator_31 (.a(inst[14:12]), .b(3'b110), .eq(comparator_31_eq));  // open: gt, lt
  Comparator #(.width(7)) comparator_32 (.a(inst[6:0]), .b(7'b0100011), .eq(MemRW));  // open: gt, lt
  Comparator #(.width(3)) comparator_33 (.a(and_22_out), .b(3'b010), .eq(comparator_33_eq));  // open: gt, lt
  or or_4 (or_4_out, comparator_27_eq, comparator_28_eq);
  assign bit_extender_12_out = {{3{comparator_29_eq}}, comparator_29_eq};  // Bit_Extender bit_extender_12
  Comparator #(.width(7)) comparator_34 (.a(inst[6:0]), .b(7'b0000011), .eq(comparator_34_eq));  // open: gt, lt
  Comparator #(.width(7)) comparator_35 (.a(inst[6:0]), .b(7'b0110011), .eq(comparator_35_eq));  // open: gt, lt
  Comparator #(.width(7)) comparator_36 (.a(inst[6:0]), .b(7'b0010111), .eq(comparator_36_eq));  // open: gt, lt
  Comparator #(.width(7)) comparator_37 (.a(inst[6:0]), .b(7'b0010011), .eq(comparator_37_eq));  // open: gt, lt
  or or_5 (ASel, comparator_24_eq, comparator_25_eq, comparator_26_eq);
  Comparator #(.width(7)) comparator_38 (.a(inst[6:0]), .b(7'b0110011), .eq(comparator_38_eq));  // open: gt, lt
  Comparator #(.width(7)) comparator_39 (.a(inst[6:0]), .b(7'b0010011), .eq(comparator_39_eq));  // open: gt, lt
  assign and_23_out = bit_extender_12_out & 4'b1101;  // AND_Gate and_23, 4 bits wide
  assign bit_extender_13_out = {{1{comparator_34_eq}}, comparator_34_eq};  // Bit_Extender bit_extender_13
  assign bit_extender_14_out = {{1{comparator_35_eq}}, comparator_35_eq};  // Bit_Extender bit_extender_14
  assign bit_extender_15_out = {{1{comparator_36_eq}}, comparator_36_eq};  // Bit_Extender bit_extender_15
  assign bit_extender_16_out = {{1{comparator_37_eq}}, comparator_37_eq};  // Bit_Extender bit_extender_16
  or or_6 (BrUn, comparator_30_eq, 1'b0, comparator_31_eq);
  Comparator #(.width(7)) comparator_40 (.a(inst[6:0]), .b(7'b0010011), .eq(comparator_40_eq));  // open: gt, lt
  Comparator #(.width(7)) comparator_41 (.a(inst[6:0]), .b(7'b1100011), .eq(comparator_41_eq));  // open: gt, lt
  Comparator #(.width(7)) comparator_42 (.a(inst[6:0]), .b(7'b1101111), .eq(comparator_42_eq));  // open: gt, lt
  Comparator #(.width(7)) comparator_43 (.a(inst[6:0]), .b(7'b0000011), .eq(comparator_43_eq));  // open: gt, lt
  Comparator #(.width(7)) comparator_44 (.a(inst[6:0]), .b(7'b1100111), .eq(comparator_44_eq));  // open: gt, lt
  assign bit_extender_17_out = {{3{comparator_38_eq}}, comparator_38_eq};  // Bit_Extender bit_extender_17
  assign bit_extender_18_out = {{3{comparator_39_eq}}, comparator_39_eq};  // Bit_Extender bit_extender_18
  assign and_24_out = bit_extender_13_out & 2'b10;  // AND_Gate and_24, 2 bits wide
  assign and_25_out = bit_extender_14_out & 2'b01;  // AND_Gate and_25, 2 bits wide
  assign and_26_out = bit_extender_15_out & 2'b01;  // AND_Gate and_26, 2 bits wide
  assign and_27_out = bit_extender_16_out & 2'b01;  // AND_Gate and_27, 2 bits wide
  assign WBSel = and_24_out | and_25_out | and_21_out | and_26_out | and_27_out;  // OR_Gate or_7, 2 bits wide
  or or_8 (BSel, comparator_40_eq, comparator_33_eq, comparator_41_eq, or_4_out, comparator_42_eq, comparator_43_eq, comparator_44_eq);
  assign and_28_out = bit_extender_17_out & ALUSelR;  // AND_Gate and_28, 4 bits wide
  assign and_29_out = bit_extender_18_out & ALUSelI;  // AND_Gate and_29, 4 bits wide
  assign ALUSel = and_28_out | and_29_out | and_23_out;  // OR_Gate or_9, 4 bits wide
  Comparator #(.width(7)) comparator_45 (.a(inst[6:0]), .b(7'b1100111), .eq(comparator_45_eq));  // open: gt, lt
  Comparator #(.width(7)) comparator_46 (.a(inst[6:0]), .b(7'b1101111), .eq(comparator_46_eq));  // open: gt, lt
  Comparator #(.width(4)) comparator_47 (
    .a({inst[14:12], inst[30]}), .b(4'b1011), .eq(comparator_47_eq));  // open: gt, lt
  Comparator #(.width(5)) comparator_48 (
    .a({inst[14:12], inst[30], inst[25]}), .b(5'b01101), .eq(comparator_48_eq));  // open: gt, lt
  Comparator #(.width(5)) comparator_49 (
    .a({inst[14:12], inst[30], inst[25]}), .b({5{1'b0}}), .eq(comparator_49_eq));  // open: gt, lt
  Comparator #(.width(5)) comparator_50 (
    .a({inst[14:12], inst[30], inst[25]}), .b(5'b00001), .eq(comparator_50_eq));  // open: gt, lt
  Comparator #(.width(5)) comparator_51 (
    .a({inst[14:12], inst[30], inst[25]}), .b(5'b00010), .eq(comparator_51_eq));  // open: gt, lt
  Comparator #(.width(5)) comparator_52 (
    .a({inst[14:12], inst[30], inst[25]}), .b(5'b00100), .eq(comparator_52_eq));  // open: gt, lt
  Comparator #(.width(5)) comparator_53 (
    .a({inst[14:12], inst[30], inst[25]}), .b(5'b00101), .eq(comparator_53_eq));  // open: gt, lt
  Comparator #(.width(5)) comparator_54 (
    .a({inst[14:12], inst[30], inst[25]}), .b(5'b01000), .eq(comparator_54_eq));  // open: gt, lt
  Comparator #(.width(5)) comparator_55 (
    .a({inst[14:12], inst[30], inst[25]}), .b(5'b10000), .eq(comparator_55_eq));  // open: gt, lt
  Comparator #(.width(5)) comparator_56 (
    .a({inst[14:12], inst[30], inst[25]}), .b(5'b10101), .eq(comparator_56_eq));  // open: gt, lt
  Comparator #(.width(5)) comparator_57 (
    .a({inst[14:12], inst[30], inst[25]}), .b(5'b10100), .eq(comparator_57_eq));  // open: gt, lt
  Comparator #(.width(5)) comparator_58 (
    .a({inst[14:12], inst[30], inst[25]}), .b(5'b11000), .eq(comparator_58_eq));  // open: gt, lt
  Comparator #(.width(5)) comparator_59 (
    .a({inst[14:12], inst[30], inst[25]}), .b(5'b11101), .eq(comparator_59_eq));  // open: gt, lt
  Comparator #(.width(5)) comparator_60 (
    .a({inst[14:12], inst[30], inst[25]}), .b(5'b11100), .eq(comparator_60_eq));  // open: gt, lt
  or or_10 (jal_jalr_sel, comparator_45_eq, comparator_46_eq);
  assign bit_extender_19_out = {{3{comparator_47_eq}}, comparator_47_eq};  // Bit_Extender bit_extender_19
  assign bit_extender_20_out = {{3{comparator_48_eq}}, comparator_48_eq};  // Bit_Extender bit_extender_20
  assign bit_extender_21_out = {{3{comparator_49_eq}}, comparator_49_eq};  // Bit_Extender bit_extender_21
  assign bit_extender_22_out = {{3{comparator_50_eq}}, comparator_50_eq};  // Bit_Extender bit_extender_22
  assign bit_extender_23_out = {{3{comparator_51_eq}}, comparator_51_eq};  // Bit_Extender bit_extender_23
  assign bit_extender_24_out = {{3{comparator_52_eq}}, comparator_52_eq};  // Bit_Extender bit_extender_24
  assign bit_extender_25_out = {{3{comparator_53_eq}}, comparator_53_eq};  // Bit_Extender bit_extender_25
  assign bit_extender_26_out = {{3{comparator_54_eq}}, comparator_54_eq};  // Bit_Extender bit_extender_26
  assign bit_extender_27_out = {{3{comparator_55_eq}}, comparator_55_eq};  // Bit_Extender bit_extender_27
  assign bit_extender_28_out = {{3{comparator_56_eq}}, comparator_56_eq};  // Bit_Extender bit_extender_28
  assign bit_extender_29_out = {{3{comparator_57_eq}}, comparator_57_eq};  // Bit_Extender bit_extender_29
  assign bit_extender_30_out = {{3{comparator_58_eq}}, comparator_58_eq};  // Bit_Extender bit_extender_30
  assign bit_extender_31_out = {{3{comparator_59_eq}}, comparator_59_eq};  // Bit_Extender bit_extender_31
  assign bit_extender_32_out = {{3{comparator_60_eq}}, comparator_60_eq};  // Bit_Extender bit_extender_32
  assign and_30_out = bit_extender_19_out & 4'b0101;  // AND_Gate and_30, 4 bits wide
  assign and_31_out = bit_extender_20_out & 4'b1011;  // AND_Gate and_31, 4 bits wide
  assign and_32_out = bit_extender_21_out & 4'b0000;  // AND_Gate and_32, 4 bits wide
  assign and_33_out = bit_extender_22_out & 4'b1010;  // AND_Gate and_33, 4 bits wide
  assign and_34_out = bit_extender_23_out & 4'b1100;  // AND_Gate and_34, 4 bits wide
  assign and_35_out = bit_extender_24_out & 4'b0110;  // AND_Gate and_35, 4 bits wide
  assign and_36_out = bit_extender_25_out & 4'b1110;  // AND_Gate and_36, 4 bits wide
  assign and_37_out = bit_extender_26_out & 4'b0111;  // AND_Gate and_37, 4 bits wide
  assign and_38_out = bit_extender_27_out & 4'b0011;  // AND_Gate and_38, 4 bits wide
  assign and_39_out = bit_extender_28_out & 4'b1000;  // AND_Gate and_39, 4 bits wide
  assign and_40_out = bit_extender_29_out & 4'b0100;  // AND_Gate and_40, 4 bits wide
  assign and_41_out = bit_extender_30_out & 4'b0010;  // AND_Gate and_41, 4 bits wide
  assign and_42_out = bit_extender_31_out & 4'b1001;  // AND_Gate and_42, 4 bits wide
  assign and_43_out = bit_extender_32_out & 4'b0001;  // AND_Gate and_43, 4 bits wide
  Comparator #(.width(3)) comparator_61 (.a(inst[14:12]), .b(3'b101), .eq(comparator_61_eq));  // open: gt, lt
  Comparator #(.width(3)) comparator_62 (.a(inst[14:12]), .b(3'b000), .eq(comparator_62_eq));  // open: gt, lt
  Comparator #(.width(3)) comparator_63 (.a(inst[14:12]), .b(3'b100), .eq(comparator_63_eq));  // open: gt, lt
  Comparator #(.width(3)) comparator_64 (.a(inst[14:12]), .b(3'b110), .eq(comparator_64_eq));  // open: gt, lt
  Comparator #(.width(3)) comparator_65 (.a(inst[14:12]), .b(3'b001), .eq(comparator_65_eq));  // open: gt, lt
  Comparator #(.width(3)) comparator_66 (.a(inst[14:12]), .b(3'b111), .eq(comparator_66_eq));  // open: gt, lt
  not not_1 (not_1_out, BrLt);
  not not_2 (not_2_out, BrEq);
  not not_3 (not_3_out, BrLt);
  and and_44 (and_44_out, comparator_61_eq, not_1_out);
  and and_45 (and_45_out, comparator_62_eq, BrEq);
  and and_46 (and_46_out, comparator_63_eq, BrLt);
  and and_47 (and_47_out, comparator_64_eq, BrLt);
  and and_48 (and_48_out, comparator_65_eq, not_2_out);
  and and_49 (and_49_out, comparator_66_eq, not_3_out);
  assign ALUSelR = and_30_out | and_31_out | and_32_out | and_33_out | and_34_out | and_35_out | and_36_out | and_37_out | and_38_out | and_39_out | and_40_out | and_41_out | and_42_out | and_43_out | 4'b0000;  // OR_Gate or_11, 4 bits wide
  or or_12 (or_12_out, and_44_out, and_45_out, and_46_out, and_47_out, and_48_out, and_49_out);
  Comparator #(.width(7)) comparator_67 (.a(inst[6:0]), .b(7'b1100011), .eq(comparator_67_eq));  // open: gt, lt
  and and_50 (and_50_out, comparator_67_eq, or_12_out);
  or or_13 (PCSel, and_50_out, jal_jalr_sel);
  Comparator #(.width(3)) comparator_68 (.a(inst[14:12]), .b(3'b000), .eq(comparator_68_eq));  // open: gt, lt
  Comparator #(.width(3)) comparator_69 (.a(inst[14:12]), .b(3'b001), .eq(comparator_69_eq));  // open: gt, lt
  Comparator #(.width(3)) comparator_70 (.a(inst[14:12]), .b(3'b010), .eq(comparator_70_eq));  // open: gt, lt
  Comparator #(.width(3)) comparator_71 (.a(inst[14:12]), .b(3'b100), .eq(comparator_71_eq));  // open: gt, lt
  Comparator #(.width(3)) comparator_72 (.a(inst[14:12]), .b(3'b101), .eq(comparator_72_eq));  // open: gt, lt
  Comparator #(.width(4)) comparator_73 (
    .a({inst[14:12], inst[30]}), .b(4'b1011), .eq(comparator_73_eq));  // open: gt, lt
  Comparator #(.width(3)) comparator_74 (.a(inst[14:12]), .b(3'b110), .eq(comparator_74_eq));  // open: gt, lt
  Comparator #(.width(3)) comparator_75 (.a(inst[14:12]), .b(3'b111), .eq(comparator_75_eq));  // open: gt, lt
  assign bit_extender_33_out = {{3{comparator_68_eq}}, comparator_68_eq};  // Bit_Extender bit_extender_33
  assign bit_extender_34_out = {{3{comparator_69_eq}}, comparator_69_eq};  // Bit_Extender bit_extender_34
  assign bit_extender_35_out = {{3{comparator_70_eq}}, comparator_70_eq};  // Bit_Extender bit_extender_35
  assign bit_extender_36_out = {{3{comparator_71_eq}}, comparator_71_eq};  // Bit_Extender bit_extender_36
  assign bit_extender_37_out = {{3{comparator_72_eq}}, comparator_72_eq};  // Bit_Extender bit_extender_37
  assign bit_extender_38_out = {{3{comparator_73_eq}}, comparator_73_eq};  // Bit_Extender bit_extender_38
  assign bit_extender_39_out = {{3{comparator_74_eq}}, comparator_74_eq};  // Bit_Extender bit_extender_39
  assign bit_extender_40_out = {{3{comparator_75_eq}}, comparator_75_eq};  // Bit_Extender bit_extender_40
  assign and_51_out = bit_extender_33_out & 4'b0000;  // AND_Gate and_51, 4 bits wide
  assign and_52_out = bit_extender_34_out & 4'b0110;  // AND_Gate and_52, 4 bits wide
  assign and_53_out = bit_extender_35_out & 4'b0111;  // AND_Gate and_53, 4 bits wide
  assign and_54_out = bit_extender_36_out & 4'b0011;  // AND_Gate and_54, 4 bits wide
  assign and_55_out = bit_extender_37_out & 4'b0100;  // AND_Gate and_55, 4 bits wide
  assign and_56_out = bit_extender_38_out & 4'b0101;  // AND_Gate and_56, 4 bits wide
  assign and_57_out = bit_extender_39_out & 4'b0010;  // AND_Gate and_57, 4 bits wide
  assign and_58_out = bit_extender_40_out & 4'b0001;  // AND_Gate and_58, 4 bits wide
  assign out_13 = {{3{1'b1}}, 1'b1};  // Bit_Extender bit_extender_41
  assign ALUSelI = and_51_out | and_52_out | and_53_out | and_54_out | and_55_out | and_56_out | and_57_out | and_58_out;  // OR_Gate or_14, 4 bits wide

  assign out_14 = 5'b00010;

  // Other names for the same wires on the sheet: funct7[6:0] = inst[31:25];
  //   SEL[4:0] = {inst[14:12], inst[30], inst[25]}; SELI[3:0] = {inst[14:12], inst[30]}; funct3[2:0] = inst[14:12];
  //   opcode[6:0] = inst[6:0]; rd[4:0] = inst[11:7]; rs1[4:0] = inst[19:15]; rs2[4:0] = inst[24:20]

  // Notes on the sheet:
  //   INPUTS to your circuit
  //   DON'T CHANGE THE LOCATIONS OF THE INPUTS AND OUTPUTS!
  //   OUTPUT from your circuit
  //   sra
  //   mulhu
  //   add
  //   mul
  //   sub
  //   sll
  //   mulh
  //   slt
  //   xor
  //   divu
  //   srl
  //   or
  //   remu
  //   and
  //   bge
  //   beq
  //   blt
  //   bltu
  //   bne
  //   bgeu
  //   R型
  //   addi
  //   slli
  //   slti
  //   xori
  //   srli
  //   srai
  //   ori
  //   andi
  //   I型
endmodule
