// Logisim project cpu.circ as structural Verilog: 1 circuit, main circuit main
module main (
  input  [31:0] INSTRUCTION,
  input  CLOCK,
  output [31:0] PROGRAM_COUNTER,
  output [31:0] ra,
  output [31:0] sp,
  output [31:0] t0,
  output [31:0] t1,
  output [31:0] t2,
  output [31:0] s0,
  output [31:0] s1,
  output [31:0] a0,
  output [31:0] out_12,
  output [31:0] out_13,
  output [31:0] out_14,
  output [31:0] out_15,
  output [31:0] out_16,
  output [31:0] out_17,
  output [31:0] out_18,
  output [3:0] out_19,
  output [2:0] out_20,
  output [31:0] out_21
);

  wire ASel, BrEq, BrLi, BrUn, BSel, comparator_1_eq, comparator_2_eq, comparator_3_eq, DMEM_p1, DMEM_p5,
       MemRW, PCSel, RegWEn;
  wire [1:0] WBSel;
  wire [2:0] ImmSel;
  wire [31:0] adder_1_out, adder_2_out, and_1_out, and_2_out, and_3_out, bit_extender_1_out,
       bit_extender_2_out, bit_extender_3_out, bit_extender_4_out, bit_extender_5_out, multiplexer_1_out,
       multiplexer_2_out, multiplexer_3_out, multiplexer_4_out, PC_EX, RD_WB, Read_data;

  // control_logic control_logic_1: pin names not known; wires that end beside it: PCSel, out_21, RegWEn, ImmSel, out_20, BrUn, BrEq, BrLi, ASel, BSel, out_19, MemRW, WBSel
  Adder #(.width(32)) adder_1 (.a(PROGRAM_COUNTER), .b(32'h4), .out(adder_1_out));  // open: cin, cout
  Multiplexer #(.width(32), .enable("false")) multiplexer_1 (
    .in0(adder_1_out), .in1(out_15), .out(multiplexer_1_out), .sel(PCSel));
  imm_gen imm_gen_1 (.ImmSel(ImmSel), .imm(out_16), .inst(out_21));
  Register #(.width(32)) PC (.D(multiplexer_1_out), .clk(CLOCK), .Q(PROGRAM_COUNTER));  // open: en, clr
  Multiplexer #(.width(32), .enable("false")) multiplexer_2 (
    .in0(INSTRUCTION), .in1(32'h13), .out(multiplexer_2_out), .sel(PCSel));
  Register #(.width(32)) register_1 (.D(multiplexer_2_out), .en(1'b1), .clk(CLOCK), .Q(out_21));  // open: clr
  Register #(.width(32)) register_2 (.D(PROGRAM_COUNTER), .en(1'b1), .clk(CLOCK), .Q(PC_EX));  // open: clr
  regfile_main RegFile (
    .rs2(out_21[24:20]), .rd(out_21[11:7]), .Read_Data_1(out_13), .Read_Data_2(out_18), .ra(ra), .sp(sp),
    .t0(t0), .t1(t1), .t2(t2), .s0(s0), .s1(s1), .a0(a0), .rs1(out_21[19:15]), .Write_Data(out_12),
    .RegWEn(RegWEn), .clk(CLOCK));
  Multiplexer #(.width(32), .enable("false")) multiplexer_3 (
    .in0(out_13), .in1(PC_EX), .out(multiplexer_3_out), .sel(ASel));
  Multiplexer #(.width(32), .enable("false")) multiplexer_4 (
    .in0(out_18), .in1(out_16), .out(multiplexer_4_out), .sel(BSel));
  alu Arithmetic_Logic_Unit (.Result(out_15), .ALUSel(out_19), .A(multiplexer_3_out), .B(multiplexer_4_out));
  Comparator #(.width(3)) comparator_1 (.a(out_21[14:12]), .b(3'b001), .eq(comparator_1_eq));  // open: gt, lt
  Comparator #(.width(3)) comparator_2 (.a(out_21[14:12]), .b(3'b000), .eq(comparator_2_eq));  // open: gt, lt
  Comparator #(.width(3)) comparator_3 (.a(out_21[14:12]), .b(3'b010), .eq(comparator_3_eq));  // open: gt, lt
  assign bit_extender_1_out = {{16{Read_data[15]}}, Read_data[15:0]};  // Bit_Extender bit_extender_1
  assign bit_extender_2_out = {{31{comparator_1_eq}}, comparator_1_eq};  // Bit_Extender bit_extender_2
  assign bit_extender_3_out = {{24{Read_data[7]}}, Read_data[7:0]};  // Bit_Extender bit_extender_3
  assign bit_extender_4_out = {{31{comparator_2_eq}}, comparator_2_eq};  // Bit_Extender bit_extender_4
  assign bit_extender_5_out = {{31{comparator_3_eq}}, comparator_3_eq};  // Bit_Extender bit_extender_5
  branch_comp branch_comp_1 (.BrEq(BrEq), .BrUn(BrUn), .rs1(out_13), .BrLt(BrLi), .rs2(out_18));
  assign and_1_out = bit_extender_1_out & bit_extender_2_out;  // AND_Gate and_1, 32 bits wide
  assign and_2_out = bit_extender_3_out & bit_extender_4_out;  // AND_Gate and_2, 32 bits wide
  assign and_3_out = Read_data & bit_extender_5_out;  // AND_Gate and_3, 32 bits wide
  // mem_main DMEM: pin names not known; wires that end beside it: DMEM_p1, DMEM_p1, out_15, out_18, DMEM_p5, CLOCK, MemRW, Read_data
  assign RD_WB = and_1_out | and_2_out | and_3_out;  // OR_Gate or_1, 32 bits wide
  Adder #(.width(32)) adder_2 (.a(PC_EX), .b(32'h4), .out(adder_2_out));  // open: cin, cout
  Multiplexer #(.select(2), .width(32), .enable("false")) multiplexer_5 (
    .in0(adder_2_out), .in1(out_15), .in2(RD_WB), .out(out_12), .sel(WBSel));  // open: in3

  assign out_14 = out_13;
  assign out_17 = out_16;

  // Other names for the same wires on the sheet: alu_re[31:0] = out_15; ALUSel[3:0] = out_19; clk = CLOCK;
  //   imm[31:0] = out_16; inst_EX[31:0] = out_21; opcode[6:0] = out_21[6:0]; rd_ins[4:0] = out_21[11:7];
  //   funct3[2:0] = out_21[14:12]; rs1_ins[4:0] = out_21[19:15]; rs2_ins[4:0] = out_21[24:20];
  //   funct7[6:0] = out_21[31:25]; rs1[31:0] = out_13; rs2[31:0] = out_18; WB[31:0] = out_12

  // Notes on the sheet:
  //   Output
  //   IMEM (do **NOT** move this)
  //   Inputs
  //   It is OK to move the PC, RegFile, ALU, MEM, Branch Comp, Imm Gen, and Control Logic to wherever is most convenient for you when constructing your CPU, and to delete this text
  //   Inputs/Outputs for testing. Do **NOT** move these.
endmodule
